# Fritzing sketch Fritzing Breadboard Schematic (saved by Fritzing 0.9.3b)
breadboards: 1

parts:
  U1 = NodeMCU V3.0
  NEOPIXEL1 = Neopixel Strip -- White (60/m)
  TTP223B2 = TTP223B Capacitive Touch Sensor Module
  TTP223B3 = TTP223B Capacitive Touch Sensor Module
  Squix1 = OLED 0.96" 128x64 I2C SSD1306

nets:
  N1: U1.D1, NEOPIXEL1.+5V
  N2: U1.D2, TTP223B2.SIG
  N3: U1.D3, Squix1.SCA
  GND: U1.GND#6, U1.GND#13, U1.GND#16, U1.GND#33, NEOPIXEL1.GND, TTP223B2.GND, TTP223B3.GND, Squix1.GND
  N4: U1.D5, Squix1.SCL
  N5: U1.D6, TTP223B3.SIG
  VCC: U1.Vin, NEOPIXEL1.DI, TTP223B2.VCC, TTP223B3.VCC, Squix1.VCC

custom parts:
  NodeMCU V3.0: ESP8266 based NodeMCU
  Neopixel Strip -- White (60/m): Neopixel Strip, White, 60 pixels per meter.
  TTP223B Capacitive Touch Sensor Module: The TTP223B capacitive touch sensor module uses the TTP223B IC. The appropriate voltage is approximately 2 to 5.5 volts.
